# Fritzing sketch Untitled Sketch (saved by Fritzing 0.9.3b)
breadboards: 1

parts:
  IC1 = SELECTOR_MULTIPLEXER [package=dil16]
  IC3 = SELECTOR_MULTIPLEXER [package=dil16]
  Part1 = Arduino Leonardo (Rev3b)
  V1 = DC Power [voltage=5]
  IC4 = SELECTOR_MULTIPLEXER [package=dil16]
  IC5 = SELECTOR_MULTIPLEXER [package=dil16]
  Part2 = MPR121 Breakout
  IC2 = SELECTOR_MULTIPLEXER [package=dil16]
  IC22 = SELECTOR_MULTIPLEXER [package=dil16]
  IC23 = SELECTOR_MULTIPLEXER [package=dil16]
  IC24 = SELECTOR_MULTIPLEXER [package=dil16]
  IC25 = SELECTOR_MULTIPLEXER [package=dil16]
  IC26 = SELECTOR_MULTIPLEXER [package=dil16]
  IC27 = SELECTOR_MULTIPLEXER [package=dil16]
  IC28 = SELECTOR_MULTIPLEXER [package=dil16]
  IC29 = SELECTOR_MULTIPLEXER [package=dil16]
  IC30 = SELECTOR_MULTIPLEXER [package=dil16]
  IC31 = SELECTOR_MULTIPLEXER [package=dil16]
  IC32 = SELECTOR_MULTIPLEXER [package=dil16]
  IC33 = SELECTOR_MULTIPLEXER [package=dil16]
  IC20 = SELECTOR_MULTIPLEXER [package=dil16]

nets:
  A1/A2/A3/A4/Bot_SEL/SEL/Top_SEL: IC1.A_!A!_B, IC1.A_G, Part1.A2, Part1.A3, Part1.A4, Part1.A5, Part1.D9_PWM/A9, Part1.D10_PWM/A10, Part1.D13_PWM, IC4.A_!A!_B, IC4.A_G, IC5.A_!A!_B, IC5.A_G, IC2.A_!A!_B, IC2.A_G, IC22.A_!A!_B, IC22.A_G, IC23.A_!A!_B, IC23.A_G, IC24.A_!A!_B, IC24.A_G, IC25.A_!A!_B, IC25.A_G, IC26.A_!A!_B, IC26.A_G, IC27.A_!A!_B, IC27.A_G, IC28.A_!A!_B, IC28.A_G, IC29.A_!A!_B, IC29.A_G, IC30.A_!A!_B, IC30.A_G, IC31.A_!A!_B, IC31.A_G, IC32.A_!A!_B, IC32.A_G, IC33.A_!A!_B, IC33.A_G
  NE1: IC1.A_1Y, IC4.A_1Y, IC5.A_1Y, IC2.A_1Y, IC20.A_1A
  NE2: IC1.A_2Y, IC4.A_2Y, IC5.A_2Y, IC2.A_2Y, IC20.A_1B
  GND: IC1.P_GND, IC3.P_GND, Part1.GND, V1.V-, IC4.P_GND, IC5.P_GND, Part2.GND, IC2.P_GND, IC22.P_GND, IC23.P_GND, IC24.P_GND, IC25.P_GND, IC26.P_GND, IC27.P_GND, IC28.P_GND, IC29.P_GND, IC30.P_GND, IC31.P_GND, IC32.P_GND, IC33.P_GND, IC20.P_GND
  NE3: IC1.A_3Y, IC4.A_3Y, IC5.A_3Y, IC2.A_3Y, IC20.A_2A
  NE4: IC1.A_4Y, IC4.A_4Y, IC5.A_4Y, IC2.A_4Y, IC20.A_2B
  5V: IC1.P_VCC, Part1.VIN, V1.V+, IC4.P_VCC, IC5.P_VCC, IC2.P_VCC, IC22.P_VCC, IC23.P_VCC, IC24.P_VCC, IC25.P_VCC, IC26.P_VCC, IC27.P_VCC, IC28.P_VCC, IC29.P_VCC, IC30.P_VCC, IC31.P_VCC, IC32.P_VCC, IC33.P_VCC
  E/W_SEL: IC3.A_!A!_B, Part1.D11_PWM, IC20.A_!A!_B
  NW1: IC3.A_1A, IC26.A_1Y, IC27.A_1Y, IC32.A_1Y, IC33.A_1Y
  NW2: IC3.A_1B, IC26.A_2Y, IC27.A_2Y, IC32.A_2Y, IC33.A_2Y
  DATA: IC3.A_1Y, IC3.A_2Y, IC3.A_3Y, IC3.A_4Y, Part1.D12/A11, IC20.A_1Y, IC20.A_2Y, IC20.A_3Y, IC20.A_4Y
  NW3: IC3.A_2A, IC26.A_3Y, IC27.A_3Y, IC32.A_3Y, IC33.A_3Y
  NW4: IC3.A_2B, IC26.A_4Y, IC27.A_4Y, IC32.A_4Y, IC33.A_4Y
  SW2: IC3.A_3B, IC28.A_2Y, IC29.A_2Y, IC30.A_2Y, IC31.A_2Y
  SW1: IC3.A_3A, IC28.A_1Y, IC29.A_1Y, IC30.A_1Y, IC31.A_1Y
  SW4: IC3.A_4B, IC28.A_4Y, IC29.A_4Y, IC30.A_4Y, IC31.A_4Y
  SW3: IC3.A_4A, IC28.A_3Y, IC29.A_3Y, IC30.A_3Y, IC31.A_3Y
  N1: IC3.A_G, Part1.D7
  N2: Part1.D6_PWM/A7, IC20.A_G
  3V3: Part1.3V3, Part2.3.3V
  SE1: IC22.A_1Y, IC23.A_1Y, IC24.A_1Y, IC25.A_1Y, IC20.A_3A
  SE2: IC22.A_2Y, IC23.A_2Y, IC24.A_2Y, IC25.A_2Y, IC20.A_3B
  SE3: IC22.A_3Y, IC23.A_3Y, IC24.A_3Y, IC25.A_3Y, IC20.A_4A
  SE4: IC22.A_4Y, IC23.A_4Y, IC24.A_4Y, IC25.A_4Y, IC20.A_4B

notes:
  NE
  each individual tile square
  letters
  east

// code stored in the sketch: patchReader.ino
/*

2 pins control enable the east and west side of the board, 
and the following 4 pins enable one of 4 chips in each quadrant. 
using E/W_SEL and SEL, you can control which of 8 lines you can 
get data from. I can explain in more depth later, but this will be 
how each tile is read.
*/
void setup (){
int [8] pins; 
pinMode(D6 , INPUT); //east
pinMode(D7 , INPUT); //west
pinMode(A2 , INPUT); //tile 1
pinMode(A3 , INPUT); //tile 2
pinMode(A4 , INPUT); //tile 3
pinMode(A1 , INPUT); //tile 4

//pins to control  for reading
pinMode (D13, OUTPUT); //sel
pinMode (D11, OUTPUT); //e/w_sel
pinMode (D10, OUTPUT); //top sel
pinMode (D9, OUTPUT);//bot sel

pinMode (D12, INPUT)//read input data from this pin (a or b input)

}
void loop(){
	tile_sel(1,4); //east, bottom right 
	Serial.println(pins);
	
}

void tile_sel(int is_east, int cardinal){
if (is_east){
	pins[0] = 1;//east?
	pins [1] = 0;//west?
	digitalWrite(D7, LOW);//set west to low
	digitalWrite(D6, HIGH);//set west to low
}
else{
	pins[0] = 0;//east?
	pins [1] = 1;//west?
	digitalWrite(D7, HIGH);//set west to low
	digitalWrite(D6, HIGH);//set west to low
}

switch (cardinal){
	case 1: //top left
		pins [2] = 1;
		pins [3] = 0;
		pins [4] = 0;
		pins [5] = 0;
	break;

	case 2://top right
		pins [2] = 1;
		pins [3] = 0;
		pins [4] = 0;
		pins [5] = 0;
	break;

	case 3://bottom left
		pins [2] = 1;
		pins [3] = 0;
		pins [4] = 0;
		pins [5] = 0;
	break;

	case 4://bottom right
		pins [2] = 1;
		pins [3] = 0;
		pins [4] = 0;
		pins [5] = 0;
	break;
	default: Serial.println("invalid input!");

}
//set e/w sel

}
